// Digital circuit adder-8bit.dig as structural Verilog
module adder_8bit (
  input  A1,
  input  B1,
  input  A2,
  input  B2,
  input  A3,
  input  B3,
  input  A4,
  input  B4,
  input  A5,
  input  B5,
  input  A6,
  input  B6,
  input  A7,
  input  B7,
  input  A8,
  input  B8,
  output S1,
  output S2,
  output S3,
  output S4,
  output S5,
  output S6,
  output S7,
  output S8,
  output ov
);

  wire full_adder_1bit_1_p5, full_adder_1bit_2_p5, full_adder_1bit_3_p5, full_adder_1bit_4_p5,
       full_adder_1bit_5_p5, full_adder_1bit_6_p5, full_adder_1bit_7_p5;

  // full_adder_1bit full_adder_1bit_1: pin names not known; wires that end beside it: A1, B1, 1'b0, S1, full_adder_1bit_1_p5
  // full_adder_1bit full_adder_1bit_2: pin names not known; wires that end beside it: A2, B2, full_adder_1bit_1_p5, S2, full_adder_1bit_2_p5
  // full_adder_1bit full_adder_1bit_3: pin names not known; wires that end beside it: A3, B3, full_adder_1bit_2_p5, S3, full_adder_1bit_3_p5
  // full_adder_1bit full_adder_1bit_4: pin names not known; wires that end beside it: A4, B4, full_adder_1bit_3_p5, S4, full_adder_1bit_4_p5
  // full_adder_1bit full_adder_1bit_5: pin names not known; wires that end beside it: A5, B5, full_adder_1bit_4_p5, S5, full_adder_1bit_5_p5
  // full_adder_1bit full_adder_1bit_6: pin names not known; wires that end beside it: A6, B6, full_adder_1bit_5_p5, S6, full_adder_1bit_6_p5
  // full_adder_1bit full_adder_1bit_7: pin names not known; wires that end beside it: A7, B7, full_adder_1bit_6_p5, S7, full_adder_1bit_7_p5
  // full_adder_1bit full_adder_1bit_8: pin names not known; wires that end beside it: A8, B8, full_adder_1bit_7_p5, S8, ov
endmodule
