// Digital circuit multiplier-4bit.dig as structural Verilog
module multiplier_4bit (
  input  B1,
  input  B2,
  input  B3,
  input  B4,
  input  A1,
  input  A2,
  input  A3,
  input  A4,
  output P1,
  output P2,
  output P3,
  output P4,
  output P5,
  output P6,
  output P7,
  output P8
);

  wire and_1_out, and_2_out, and_3_out, and_4_out, and_5_out, and_9_out, and_10_out, and_12_out, and_13_out,
       and_14_out, and_15_out, full_adder_1bit_1_p1, full_adder_1bit_1_p2, full_adder_1bit_2_p1,
       full_adder_1bit_2_p2, full_adder_1bit_2_p5, full_adder_1bit_3_p1, full_adder_1bit_4_p1,
       full_adder_1bit_4_p2, full_adder_1bit_4_p4, full_adder_1bit_4_p5, full_adder_1bit_5_p1,
       full_adder_1bit_5_p5, full_adder_1bit_6_p1, full_adder_1bit_6_p4, full_adder_1bit_7_p1,
       full_adder_1bit_7_p4, full_adder_1bit_7_p5, full_adder_1bit_8_p1, full_adder_1bit_8_p5,
       half_adder_1bit_1_p1, half_adder_1bit_1_p4;

  and and_1 (and_1_out, A4, B4);
  // full_adder_1bit full_adder_1bit_1: pin names not known; wires that end beside it: full_adder_1bit_1_p1, full_adder_1bit_1_p2, P8, and_1_out, P7
  and and_2 (and_2_out, A4, B3);
  // full_adder_1bit full_adder_1bit_2: pin names not known; wires that end beside it: full_adder_1bit_2_p1, full_adder_1bit_2_p2, full_adder_1bit_1_p2, and_2_out, full_adder_1bit_2_p5
  and and_3 (and_3_out, A4, B2);
  // half_adder_1bit half_adder_1bit_1: pin names not known; wires that end beside it: half_adder_1bit_1_p1, full_adder_1bit_2_p2, and_3_out, half_adder_1bit_1_p4
  and and_4 (and_4_out, A3, B4);
  // full_adder_1bit full_adder_1bit_3: pin names not known; wires that end beside it: full_adder_1bit_3_p1, full_adder_1bit_2_p5, full_adder_1bit_1_p1, and_4_out, P6
  // full_adder_1bit full_adder_1bit_4: pin names not known; wires that end beside it: full_adder_1bit_4_p1, full_adder_1bit_4_p2, half_adder_1bit_1_p1, full_adder_1bit_4_p4, full_adder_1bit_4_p5
  and and_5 (and_5_out, A3, B3);
  // full_adder_1bit full_adder_1bit_5: pin names not known; wires that end beside it: full_adder_1bit_5_p1, half_adder_1bit_1_p4, full_adder_1bit_2_p1, and_5_out, full_adder_1bit_5_p5
  // full_adder_1bit full_adder_1bit_6: pin names not known; wires that end beside it: full_adder_1bit_6_p1, full_adder_1bit_5_p5, full_adder_1bit_3_p1, full_adder_1bit_6_p4, P5
  and and_6 (full_adder_1bit_4_p2, A4, B1);
  and and_7 (full_adder_1bit_4_p4, A3, B2);
  // full_adder_1bit full_adder_1bit_7: pin names not known; wires that end beside it: full_adder_1bit_7_p1, full_adder_1bit_4_p5, full_adder_1bit_5_p1, full_adder_1bit_7_p4, full_adder_1bit_7_p5
  and and_8 (full_adder_1bit_6_p4, A2, B4);
  and and_9 (and_9_out, A3, B1);
  and and_10 (and_10_out, A2, B2);
  // full_adder_1bit full_adder_1bit_8: pin names not known; wires that end beside it: full_adder_1bit_8_p1, and_9_out, full_adder_1bit_4_p1, and_10_out, full_adder_1bit_8_p5
  and and_11 (full_adder_1bit_7_p4, A2, B3);
  and and_12 (and_12_out, A1, B4);
  // half_adder_1bit half_adder_1bit_2: pin names not known; wires that end beside it: full_adder_1bit_7_p5, full_adder_1bit_6_p1, and_12_out, P4
  and and_13 (and_13_out, A2, B1);
  and and_14 (and_14_out, A1, B3);
  // half_adder_1bit half_adder_1bit_3: pin names not known; wires that end beside it: full_adder_1bit_8_p5, full_adder_1bit_7_p1, and_14_out, P3
  and and_15 (and_15_out, A1, B2);
  // half_adder_1bit half_adder_1bit_4: pin names not known; wires that end beside it: and_13_out, full_adder_1bit_8_p1, and_15_out, P2
  and and_16 (P1, A1, B1);
endmodule
