// Digital circuit subtractor-8bit.dig as structural Verilog
module subtractor_8bit (
  input  A1,
  input  A2,
  input  A3,
  input  A4,
  input  A5,
  input  A6,
  input  A7,
  input  A8,
  input  B1,
  input  B2,
  input  B3,
  input  B4,
  input  B5,
  input  B6,
  input  B7,
  input  B8,
  output S1,
  output S2,
  output S3,
  output S4,
  output S5,
  output S6,
  output S7,
  output S8,
  output Uv
);

  wire full_adder_1bit_1_p5, full_adder_1bit_2_p5, full_adder_1bit_3_p5, full_adder_1bit_4_p5,
       full_adder_1bit_5_p5, full_adder_1bit_6_p5, full_adder_1bit_7_p5, not_1_out, not_2_out, not_3_out,
       not_4_out, not_5_out, not_6_out, not_7_out, not_8_out;

  not not_1 (not_1_out, A1);
  not not_2 (not_2_out, A2);
  not not_3 (not_3_out, A3);
  not not_4 (not_4_out, A4);
  not not_5 (not_5_out, A5);
  not not_6 (not_6_out, A6);
  not not_7 (not_7_out, A7);
  not not_8 (not_8_out, A8);
  // full_adder_1bit full_adder_1bit_1: pin names not known; wires that end beside it: not_1_out, B1, 1'b1, S1, full_adder_1bit_1_p5
  // full_adder_1bit full_adder_1bit_2: pin names not known; wires that end beside it: not_2_out, B2, full_adder_1bit_1_p5, S2, full_adder_1bit_2_p5
  // full_adder_1bit full_adder_1bit_3: pin names not known; wires that end beside it: not_3_out, B3, full_adder_1bit_2_p5, S3, full_adder_1bit_3_p5
  // full_adder_1bit full_adder_1bit_4: pin names not known; wires that end beside it: not_4_out, B4, full_adder_1bit_3_p5, S4, full_adder_1bit_4_p5
  // full_adder_1bit full_adder_1bit_5: pin names not known; wires that end beside it: not_5_out, B5, full_adder_1bit_4_p5, S5, full_adder_1bit_5_p5
  // full_adder_1bit full_adder_1bit_6: pin names not known; wires that end beside it: not_6_out, B6, full_adder_1bit_5_p5, S6, full_adder_1bit_6_p5
  // full_adder_1bit full_adder_1bit_7: pin names not known; wires that end beside it: not_7_out, B7, full_adder_1bit_6_p5, S7, full_adder_1bit_7_p5
  // full_adder_1bit full_adder_1bit_8: pin names not known; wires that end beside it: not_8_out, B8, full_adder_1bit_7_p5, S8, Uv
endmodule
