// Digital circuit xor-8bit.dig as structural Verilog
module xor_8bit (
  input  A1,
  input  B1,
  input  A2,
  input  B2,
  input  A3,
  input  B3,
  input  A4,
  input  B4,
  input  A5,
  input  B5,
  input  A6,
  input  B6,
  input  A7,
  input  B7,
  input  A8,
  input  B8,
  output R1,
  output R2,
  output R3,
  output R4,
  output R5,
  output R6,
  output R7,
  output R8
);

  xor xor_1 (R1, B1, A1);
  xor xor_2 (R2, B2, A2);
  xor xor_3 (R3, B3, A3);
  xor xor_4 (R4, B4, A4);
  xor xor_5 (R5, B5, A5);
  xor xor_6 (R6, B6, A6);
  xor xor_7 (R7, B7, A7);
  xor xor_8 (R8, B8, A8);
endmodule
